// Logisim project processador_vetorial.circ as structural Verilog: 13 circuits, main circuit main
module main (
);

  wire and_1_out, and_2_out, and_3_out, button_1_out, clk, is_brzr, is_mov_escalar, is_mov_vet, is_vet,
       mem_escalar, mux_dado_breg, not_2_out, pipeline_id_ex_1_is_vet_out, pipeline_id_ex_1_mem_to_reg_out,
       pipeline_id_ex_1_wbreg_out, pipeline_id_ex_1_wm_out, reg_a_t, sel_imm, sel_mov, ula_1_brzr, WB, wbreg,
       wbreg_escalar, wbreg_EX_MEM, wm, wm_escalar, wmem, ZERO;
  wire [1:0] index_rd, index_rd_EX_MEM, opula_escalar, opula_vet, pipeline_id_ex_1_index_ra_out,
       pipeline_id_ex_1_opula_out;
  wire [2:0] opcode;
  wire [3:0] IMM_vet;
  wire [7:0] adder_1_out, D, dualram_1_p8, IMM, multiplexer_1_out, multiplexer_5_out, PC_q, reg_A,
       reg_A_EX_MEM, reg_B, reg_B_EX_MEM, sr_ra, sr_rb, ula_1_c, ULA_result, undriven;

  Multiplexer #(.width(8)) multiplexer_1 (
    .in0(adder_1_out), .in1(reg_B_EX_MEM), .out(multiplexer_1_out), .sel(and_1_out));
  and and_1 (and_1_out, ZERO, is_brzr);
  Register PC (.D(multiplexer_1_out), .clk(clk), .Q(PC_q), .clr(button_1_out));  // open: en
  Clock clock_1 (.out(clk));
  Button button_1 (.out(button_1_out));
  Adder adder_1 (.a(8'h1), .b(PC_q), .out(adder_1_out));  // open: cin, cout
  ROM #(.addrWidth(4)) rom_1 (.addr({is_vet, opcode}));  // open: data
  // DualRAM dualram_1: pin names not known; wires that end beside it: PC_q, 1'b1, clk, reg_B_EX_MEM, wmem, 1'b1, clk, dualram_1_p8
  // NOT_Gate not_1 has open pins: in=1'b1, out=open
  Register register_1 (.D(dualram_1_p8), .clk(clk), .Q({is_vet, opcode, IMM_vet}));  // open: en, clr
  Multiplexer #(.width(8)) multiplexer_2 (.in0(ULA_result), .in1(undriven), .out(D), .sel(WB));
  Multiplexer #(.width(2)) multiplexer_3 (.in0(IMM_vet[3:2]), .in1(2'b01), .out(index_rd), .sel(reg_a_t));
  Multiplexer #(.width(8)) multiplexer_4 (.in0({IMM_vet, 4'b0000}), .in1({4'b0000, IMM_vet}), .out(IMM), .sel(sel_imm));
  vet vet_1 (
    .wbreg(wbreg), .is_vet(is_vet), .wm(wm), .opula(opula_vet), .sr_ra(sr_ra), .sr_rb(sr_rb),
    .ra(IMM_vet[3:2]), .rb(IMM_vet[1:0]), .wb(mux_dado_breg), .IMM(IMM_vet), .sel_mov(sel_mov),
    .is_mov_vet(is_mov_vet), .CLK(clk));
  breg_scalar breg_scalar_1 (
    .D(D), .W(wbreg_EX_MEM), .RD(index_rd_EX_MEM), .CLK(clk), .RS1(index_rd), .RS2(IMM_vet[1:0]), .A(sr_ra),
    .B(sr_rb));
  Multiplexer #(.width(8)) multiplexer_5 (.in0(sr_ra), .in1(IMM), .out(multiplexer_5_out), .sel(is_mov_escalar));
  pipeline_ID_EX pipeline_id_ex_1 (
    .A_in(multiplexer_5_out), .B_in(sr_rb), .opula_in(opula_escalar), .index_ra_in(index_rd),
    .wbreg_in(wbreg_escalar), .is_vet_in(is_vet), .wm_in(wm_escalar), .mem_to_reg_in(mem_escalar), .CLK(clk),
    .A_out(reg_A), .B_out(reg_B), .opula_out(pipeline_id_ex_1_opula_out),
    .index_ra_out(pipeline_id_ex_1_index_ra_out), .wbreg_out(pipeline_id_ex_1_wbreg_out),
    .is_vet_out(pipeline_id_ex_1_is_vet_out), .wm_out(pipeline_id_ex_1_wm_out),
    .mem_to_reg_out(pipeline_id_ex_1_mem_to_reg_out));
  not not_2 (not_2_out, pipeline_id_ex_1_is_vet_out);
  and and_2 (and_2_out, pipeline_id_ex_1_wbreg_out, not_2_out);
  and and_3 (and_3_out, not_2_out, pipeline_id_ex_1_wm_out);
  ULA ula_1 (.A(reg_A), .B(reg_B), .OPULA(pipeline_id_ex_1_opula_out), .brzr(ula_1_brzr), .C(ula_1_c));
  Register #(.width(1)) register_2 (.D(ula_1_brzr), .clk(clk), .Q(ZERO));  // open: en, clr
  pipeline_EX_MEM pipeline_ex_mem_1 (
    .ULA_result_in(ula_1_c), .A_in(reg_A), .B_in(reg_B), .index_ra_in(pipeline_id_ex_1_index_ra_out),
    .wbreg_in(and_2_out), .wm_in(and_3_out), .mem_to_reg_in(pipeline_id_ex_1_mem_to_reg_out), .CLK(clk),
    .ULA_result_out(ULA_result), .A_out(reg_A_EX_MEM), .B_out(reg_B_EX_MEM), .index_ra_out(index_rd_EX_MEM),
    .wbreg_out(wbreg_EX_MEM), .wm_out(wmem), .mem_to_reg_out(WB));

  // Other names for the same wires on the sheet: mov_h[7:4] = IMM_vet; mov_l[3:0] = IMM_vet; rb[1:0] = IMM_vet[1:0];
  //   ra[1:0] = IMM_vet[3:2]; opcode[3] = is_vet
endmodule

module breg (
  input  [7:0] D,
  input  W,
  input  [1:0] RD,
  input  CLK,
  input  [1:0] RS1,
  input  [1:0] RS2,
  output [7:0] A,
  output [7:0] B
);

  wire W1, W2, W3, W4;
  wire [7:0] VR1, VR2, VR3, VR4;

  Demultiplexer #(.select(2)) demultiplexer_1 (.out0(W1), .out1(W2), .out2(W3), .out3(W4), .in(W), .sel(RD));
  Register register_1 (.D(D), .en(W1), .clk(CLK), .Q(VR1));  // open: clr
  Register register_2 (.D(D), .en(W2), .clk(CLK), .Q(VR2));  // open: clr
  Register register_3 (.D(D), .en(W3), .clk(CLK), .Q(VR3));  // open: clr
  Register register_4 (.D(D), .en(W4), .clk(CLK), .Q(VR4));  // open: clr
  Multiplexer #(.select(2), .width(8)) multiplexer_1 (.in0(VR1), .in1(VR2), .in2(VR3), .in3(VR4), .out(A), .sel(RS1));
  Multiplexer #(.select(2), .width(8)) multiplexer_2 (.in0(VR1), .in1(VR2), .in2(VR3), .in3(VR4), .out(B), .sel(RS2));

  // Other names for the same wires on the sheet: DADO[7:0] = D
endmodule

module ULA (
  input  [7:0] A,
  input  [7:0] B,
  input  [1:0] OPULA,
  output brzr,
  output [7:0] C
);

  wire [7:0] adder_1_out, and_1_out, subtractor_1_out;

  Adder adder_1 (.a(A), .b(B), .out(adder_1_out));  // open: cin, cout
  Subtractor subtractor_1 (.a(A), .b(B), .out(subtractor_1_out));  // open: bin, bout
  assign and_1_out = A & B;  // AND_Gate and_1, 8 bits wide
  nor nor_1 (brzr, A[0], A[1], A[2], A[3], A[4], A[5], A[6], A[7]);
  Multiplexer #(.select(2), .width(8)) multiplexer_1 (
    .in0(adder_1_out), .in1(subtractor_1_out), .in2(and_1_out), .out(C), .sel(OPULA));  // open: in3
endmodule

module breg_vet0 (
  input  [7:0] D,
  input  W,
  input  [1:0] RD,
  input  [1:0] RS1,
  input  [1:0] RS2,
  input  CLK,
  output [7:0] A,
  output [7:0] B
);

  wire W1, W2, W3;
  wire [7:0] VR1, VR2, VR3;

  Demultiplexer #(.select(2)) demultiplexer_1 (.out1(W1), .out2(W2), .out3(W3), .in(W), .sel(RD));  // open: out0
  Register register_1 (.D(D), .en(W1), .clk(CLK), .Q(VR1));  // open: clr
  Register register_2 (.D(D), .en(W2), .clk(CLK), .Q(VR2));  // open: clr
  Register register_3 (.D(D), .en(W3), .clk(CLK), .Q(VR3));  // open: clr
  Multiplexer #(.select(2), .width(8)) multiplexer_1 (
    .in0({8{1'b0}}), .in1(VR1), .in2(VR2), .in3(VR3), .out(A), .sel(RS1));
  Multiplexer #(.select(2), .width(8)) multiplexer_2 (
    .in0({8{1'b0}}), .in1(VR1), .in2(VR2), .in3(VR3), .out(B), .sel(RS2));

  // Other names for the same wires on the sheet: DADO[7:0] = D
endmodule

module breg_vet1 (
  input  [7:0] D,
  input  W,
  input  [1:0] RD,
  input  [1:0] RS1,
  input  [1:0] RS2,
  input  CLK,
  output [7:0] A,
  output [7:0] B
);

  wire W1, W2, W3;
  wire [7:0] VR1, VR2, VR3;

  Demultiplexer #(.select(2)) demultiplexer_1 (.out1(W1), .out2(W2), .out3(W3), .in(W), .sel(RD));  // open: out0
  Register register_1 (.D(D), .en(W1), .clk(CLK), .Q(VR1));  // open: clr
  Register register_2 (.D(D), .en(W2), .clk(CLK), .Q(VR2));  // open: clr
  Register register_3 (.D(D), .en(W3), .clk(CLK), .Q(VR3));  // open: clr
  Multiplexer #(.select(2), .width(8)) multiplexer_1 (.in0(8'h1), .in1(VR1), .in2(VR2), .in3(VR3), .out(A), .sel(RS1));
  Multiplexer #(.select(2), .width(8)) multiplexer_2 (.in0(8'h1), .in1(VR1), .in2(VR2), .in3(VR3), .out(B), .sel(RS2));

  // Other names for the same wires on the sheet: DADO[7:0] = D
endmodule

module breg_vet2 (
  input  [7:0] D,
  input  W,
  input  [1:0] RD,
  input  [1:0] RS1,
  input  [1:0] RS2,
  input  CLK,
  output [7:0] A,
  output [7:0] B
);

  wire W1, W2, W3;
  wire [7:0] VR1, VR2, VR3;

  Demultiplexer #(.select(2)) demultiplexer_1 (.out1(W1), .out2(W2), .out3(W3), .in(W), .sel(RD));  // open: out0
  Register register_1 (.D(D), .en(W1), .clk(CLK), .Q(VR1));  // open: clr
  Register register_2 (.D(D), .en(W2), .clk(CLK), .Q(VR2));  // open: clr
  Register register_3 (.D(D), .en(W3), .clk(CLK), .Q(VR3));  // open: clr
  Multiplexer #(.select(2), .width(8)) multiplexer_1 (.in0(8'h2), .in1(VR1), .in2(VR2), .in3(VR3), .out(A), .sel(RS1));
  Multiplexer #(.select(2), .width(8)) multiplexer_2 (.in0(8'h2), .in1(VR1), .in2(VR2), .in3(VR3), .out(B), .sel(RS2));

  // Other names for the same wires on the sheet: DADO[7:0] = D
endmodule

module breg_vet3 (
  input  [7:0] D,
  input  W,
  input  [1:0] RD,
  input  [1:0] RS1,
  input  [1:0] RS2,
  input  CLK,
  output [7:0] A,
  output [7:0] B
);

  wire W1, W2, W3;
  wire [7:0] VR1, VR2, VR3;

  Demultiplexer #(.select(2)) demultiplexer_1 (.out1(W1), .out2(W2), .out3(W3), .in(W), .sel(RD));  // open: out0
  Register register_1 (.D(D), .en(W1), .clk(CLK), .Q(VR1));  // open: clr
  Register register_2 (.D(D), .en(W2), .clk(CLK), .Q(VR2));  // open: clr
  Register register_3 (.D(D), .en(W3), .clk(CLK), .Q(VR3));  // open: clr
  Multiplexer #(.select(2), .width(8)) multiplexer_1 (.in0(8'h3), .in1(VR1), .in2(VR2), .in3(VR3), .out(A), .sel(RS1));
  Multiplexer #(.select(2), .width(8)) multiplexer_2 (.in0(8'h3), .in1(VR1), .in2(VR2), .in3(VR3), .out(B), .sel(RS2));

  // Other names for the same wires on the sheet: DADO[7:0] = D
endmodule

module breg_scalar (
  input  [7:0] D,
  input  W,
  input  [1:0] RD,
  input  CLK,
  input  [1:0] RS1,
  input  [1:0] RS2,
  output [7:0] A,
  output [7:0] B
);

  wire W2, W3, W4;
  wire [7:0] VR2, VR3, VR4;

  Demultiplexer #(.select(2)) demultiplexer_1 (.out1(W2), .out2(W3), .out3(W4), .in(W), .sel(RD));  // open: out0
  Register register_1 (.D(D), .en(W2), .clk(CLK), .Q(VR2));  // open: clr
  Register register_2 (.D(D), .en(W3), .clk(CLK), .Q(VR3));  // open: clr
  Register register_3 (.D(D), .en(W4), .clk(CLK), .Q(VR4));  // open: clr
  Multiplexer #(.select(2), .width(8)) multiplexer_1 (
    .in0({8{1'b0}}), .in1(VR2), .in2(VR3), .in3(VR4), .out(A), .sel(RS1));
  Multiplexer #(.select(2), .width(8)) multiplexer_2 (
    .in0({8{1'b0}}), .in1(VR2), .in2(VR3), .in3(VR4), .out(B), .sel(RS2));

  // Other names for the same wires on the sheet: DADO[7:0] = D
endmodule

module pipeline_ID_EX (
  input  [7:0] A_in,
  input  [7:0] B_in,
  input  [1:0] opula_in,
  input  [1:0] index_ra_in,
  input  wbreg_in,
  input  is_vet_in,
  input  wm_in,
  input  mem_to_reg_in,
  input  CLK,
  output [7:0] A_out,
  output [7:0] B_out,
  output [1:0] opula_out,
  output [1:0] index_ra_out,
  output wbreg_out,
  output is_vet_out,
  output wm_out,
  output mem_to_reg_out
);

  Register register_1 (.D(A_in), .clk(CLK), .Q(A_out));  // open: en, clr
  Register register_2 (.D(B_in), .clk(CLK), .Q(B_out));  // open: en, clr
  Register #(.width(2)) register_3 (.D(opula_in), .clk(CLK), .Q(opula_out));  // open: en, clr
  Register #(.width(2)) register_4 (.D(index_ra_in), .clk(CLK), .Q(index_ra_out));  // open: en, clr
  Register #(.width(1)) register_5 (.D(wbreg_in), .clk(CLK), .Q(wbreg_out));  // open: en, clr
  Register #(.width(1)) register_6 (.D(is_vet_in), .clk(CLK), .Q(is_vet_out));  // open: en, clr
  Register #(.width(1)) register_7 (.D(wm_in), .clk(CLK), .Q(wm_out));  // open: en, clr
  Register #(.width(1)) register_8 (.D(mem_to_reg_in), .clk(CLK), .Q(mem_to_reg_out));  // open: en, clr
endmodule

module ctrl_vet (
  input  wbreg_in,
  input  is_vet_in,
  input  wm_in,
  output wbreg_out,
  output wm_out
);

  and and_1 (wbreg_out, wbreg_in, is_vet_in);
  and and_2 (wm_out, is_vet_in, wm_in);
endmodule

module pipeline_EX_MEM (
  input  [7:0] ULA_result_in,
  input  [7:0] A_in,
  input  [7:0] B_in,
  input  [1:0] index_ra_in,
  input  wbreg_in,
  input  wm_in,
  input  mem_to_reg_in,
  input  CLK,
  output [7:0] ULA_result_out,
  output [7:0] A_out,
  output [7:0] B_out,
  output [1:0] index_ra_out,
  output wbreg_out,
  output wm_out,
  output mem_to_reg_out
);

  Register register_1 (.D(ULA_result_in), .clk(CLK), .Q(ULA_result_out));  // open: en, clr
  Register register_2 (.D(A_in), .clk(CLK), .Q(A_out));  // open: en, clr
  Register register_3 (.D(B_in), .clk(CLK), .Q(B_out));  // open: en, clr
  Register #(.width(2)) register_4 (.D(index_ra_in), .clk(CLK), .Q(index_ra_out));  // open: en, clr
  Register #(.width(1)) register_5 (.D(wbreg_in), .clk(CLK), .Q(wbreg_out));  // open: en, clr
  Register #(.width(1)) register_6 (.D(wm_in), .clk(CLK), .Q(wm_out));  // open: en, clr
  Register #(.width(1)) register_7 (.D(mem_to_reg_in), .clk(CLK), .Q(mem_to_reg_out));  // open: en, clr
endmodule

module vet (
  input  wbreg,
  input  is_vet,
  input  wm,
  input  [1:0] opula,
  input  [7:0] sr_ra,
  input  [7:0] sr_rb,
  input  [1:0] ra,
  input  [1:0] rb,
  input  wb,
  input  [3:0] IMM,
  input  sel_mov,
  input  is_mov_vet,
  input  CLK
);

  wire pipeline_id_ex_1_is_vet_out, pipeline_id_ex_1_mem_to_reg_out, pipeline_id_ex_1_wm_out,
       pipeline_id_ex_2_mem_to_reg_out, pipeline_id_ex_2_wbreg_out, pipeline_id_ex_2_wm_out,
       pipeline_id_ex_3_mem_to_reg_out, pipeline_id_ex_3_wbreg_out, pipeline_id_ex_3_wm_out,
       pipeline_id_ex_4_mem_to_reg_out, pipeline_id_ex_4_wbreg_out, pipeline_id_ex_4_wm_out, wb_0, wb_1,
       wb_2, wb_3, wbreg_0, wbreg_1, wbreg_2, wbreg_3, wbreg_ctrl_0, wbreg_ctrl_1, wbreg_ctrl_2,
       wbreg_ctrl_3, WM_ctrl_vet, WM_EX_MEM_0, WM_EX_MEM_1, WM_EX_MEM_2, WM_EX_MEM_3;
  wire [1:0] index_ra_0, index_ra_1, index_ra_2, index_ra_3, pipeline_id_ex_1_index_ra_out,
       pipeline_id_ex_1_opula_out, pipeline_id_ex_2_index_ra_out, pipeline_id_ex_2_opula_out,
       pipeline_id_ex_3_index_ra_out, pipeline_id_ex_3_opula_out, pipeline_id_ex_4_index_ra_out,
       pipeline_id_ex_4_opula_out;
  wire [7:0] A_EX_MEM_0, A_EX_MEM_1, A_EX_MEM_2, A_EX_MEM_3, adder_1_out, adder_2_out, adder_3_out,
       B_EX_MEM_0, B_EX_MEM_1, B_EX_MEM_2, B_EX_MEM_3, breg_vet0_1_a, breg_vet0_1_b, breg_vet1_1_a,
       breg_vet1_1_b, breg_vet2_1_a, breg_vet2_1_b, breg_vet3_1_a, breg_vet3_1_b, D_0, D_1, D_2, D_3,
       dualram_1_p10, dualram_2_p10, mov_result, multiplexer_2_out, multiplexer_3_out, multiplexer_4_out,
       multiplexer_5_out, ra_0, ra_1, ra_2, ra_3, rb_0, rb_1, rb_2, rb_3, ULA_0, ULA_1, ULA_2, ULA_3,
       ula_vet_1_c, ula_vet_2_c, ula_vet_3_c, ula_vet_4_c, undriven, undriven_2;

  Multiplexer #(.width(8)) multiplexer_1 (.in0({IMM, 4'b0000}), .in1({4'b0000, IMM}), .out(mov_result), .sel(sel_mov));
  ctrl_vet ctrl_vet_1 (
    .wbreg_in(wbreg), .is_vet_in(is_vet), .wm_in(wm), .wbreg_out(wbreg_ctrl_0), .wm_out(WM_ctrl_vet));
  ctrl_vet ctrl_vet_2 (
    .wbreg_in(wbreg), .is_vet_in(is_vet), .wm_in(wm), .wbreg_out(wbreg_ctrl_1), .wm_out(WM_ctrl_vet));
  ctrl_vet ctrl_vet_3 (
    .wbreg_in(wbreg), .is_vet_in(is_vet), .wm_in(wm), .wbreg_out(wbreg_ctrl_2), .wm_out(WM_ctrl_vet));
  ctrl_vet ctrl_vet_4 (
    .wbreg_in(wbreg), .is_vet_in(is_vet), .wm_in(wm), .wbreg_out(wbreg_ctrl_3), .wm_out(WM_ctrl_vet));
  breg_vet0 breg_vet0_1 (
    .D(D_0), .W(wbreg_0), .RD(index_ra_0), .RS1(ra), .RS2(rb), .CLK(CLK), .A(breg_vet0_1_a), .B(breg_vet0_1_b));
  breg_vet1 breg_vet1_1 (
    .D(D_1), .W(wbreg_1), .RD(index_ra_1), .RS1(ra), .RS2(rb), .CLK(CLK), .A(breg_vet1_1_a), .B(breg_vet1_1_b));
  breg_vet2 breg_vet2_1 (
    .D(D_2), .W(wbreg_2), .RD(index_ra_2), .RS1(ra), .RS2(rb), .CLK(CLK), .A(breg_vet2_1_a), .B(breg_vet2_1_b));
  breg_vet3 breg_vet3_1 (
    .D(D_3), .W(wbreg_3), .RD(index_ra_3), .RS1(ra), .RS2(rb), .CLK(CLK), .A(breg_vet3_1_a), .B(breg_vet3_1_b));
  Multiplexer #(.width(8)) multiplexer_2 (
    .in0(breg_vet0_1_a), .in1(mov_result), .out(multiplexer_2_out), .sel(is_mov_vet));
  Multiplexer #(.width(8)) multiplexer_3 (
    .in0(breg_vet1_1_a), .in1(mov_result), .out(multiplexer_3_out), .sel(is_mov_vet));
  Multiplexer #(.width(8)) multiplexer_4 (
    .in0(breg_vet2_1_a), .in1(mov_result), .out(multiplexer_4_out), .sel(is_mov_vet));
  Multiplexer #(.width(8)) multiplexer_5 (
    .in0(breg_vet3_1_a), .in1(mov_result), .out(multiplexer_5_out), .sel(is_mov_vet));
  pipeline_ID_EX pipeline_id_ex_1 (
    .A_in(multiplexer_2_out), .B_in(breg_vet0_1_b), .opula_in(opula), .index_ra_in(ra),
    .wbreg_in(wbreg_ctrl_0), .wm_in(WM_ctrl_vet), .mem_to_reg_in(wb), .CLK(CLK), .A_out(ra_0), .B_out(rb_0),
    .opula_out(pipeline_id_ex_1_opula_out), .index_ra_out(pipeline_id_ex_1_index_ra_out),
    .is_vet_out(pipeline_id_ex_1_is_vet_out), .wm_out(pipeline_id_ex_1_wm_out),
    .mem_to_reg_out(pipeline_id_ex_1_mem_to_reg_out));  // open: is_vet_in, wbreg_out
  pipeline_ID_EX pipeline_id_ex_2 (
    .A_in(multiplexer_3_out), .B_in(breg_vet1_1_b), .opula_in(opula), .index_ra_in(ra),
    .wbreg_in(wbreg_ctrl_1), .wm_in(WM_ctrl_vet), .mem_to_reg_in(wb), .CLK(CLK), .A_out(ra_1), .B_out(rb_1),
    .opula_out(pipeline_id_ex_2_opula_out), .index_ra_out(pipeline_id_ex_2_index_ra_out),
    .wbreg_out(pipeline_id_ex_2_wbreg_out), .wm_out(pipeline_id_ex_2_wm_out),
    .mem_to_reg_out(pipeline_id_ex_2_mem_to_reg_out));  // open: is_vet_in, is_vet_out
  pipeline_ID_EX pipeline_id_ex_3 (
    .A_in(multiplexer_4_out), .B_in(breg_vet2_1_b), .opula_in(opula), .index_ra_in(ra),
    .wbreg_in(wbreg_ctrl_2), .wm_in(WM_ctrl_vet), .mem_to_reg_in(wb), .CLK(CLK), .A_out(ra_2), .B_out(rb_2),
    .opula_out(pipeline_id_ex_3_opula_out), .index_ra_out(pipeline_id_ex_3_index_ra_out),
    .wbreg_out(pipeline_id_ex_3_wbreg_out), .wm_out(pipeline_id_ex_3_wm_out),
    .mem_to_reg_out(pipeline_id_ex_3_mem_to_reg_out));  // open: is_vet_in, is_vet_out
  pipeline_ID_EX pipeline_id_ex_4 (
    .A_in(multiplexer_5_out), .B_in(breg_vet3_1_b), .opula_in(opula), .index_ra_in(ra),
    .wbreg_in(wbreg_ctrl_3), .wm_in(WM_ctrl_vet), .mem_to_reg_in(wb), .CLK(CLK), .A_out(ra_3), .B_out(rb_3),
    .opula_out(pipeline_id_ex_4_opula_out), .index_ra_out(pipeline_id_ex_4_index_ra_out),
    .wbreg_out(pipeline_id_ex_4_wbreg_out), .wm_out(pipeline_id_ex_4_wm_out),
    .mem_to_reg_out(pipeline_id_ex_4_mem_to_reg_out));  // open: is_vet_in, is_vet_out
  ULA_vet ula_vet_1 (.A(ra_0), .B(rb_0), .OPULA(pipeline_id_ex_1_opula_out), .C(ula_vet_1_c));
  ULA_vet ula_vet_2 (.A(ra_1), .B(rb_1), .OPULA(pipeline_id_ex_2_opula_out), .C(ula_vet_2_c));
  ULA_vet ula_vet_3 (.A(ra_2), .B(rb_2), .OPULA(pipeline_id_ex_3_opula_out), .C(ula_vet_3_c));
  ULA_vet ula_vet_4 (.A(ra_3), .B(rb_3), .OPULA(pipeline_id_ex_4_opula_out), .C(ula_vet_4_c));
  pipeline_EX_MEM pipeline_ex_mem_1 (
    .ULA_result_in(ula_vet_1_c), .A_in(ra_0), .B_in(rb_0), .index_ra_in(pipeline_id_ex_1_index_ra_out),
    .wbreg_in(pipeline_id_ex_1_is_vet_out), .wm_in(pipeline_id_ex_1_wm_out),
    .mem_to_reg_in(pipeline_id_ex_1_mem_to_reg_out), .CLK(CLK), .ULA_result_out(ULA_0), .A_out(A_EX_MEM_0),
    .B_out(B_EX_MEM_0), .index_ra_out(index_ra_0), .wbreg_out(wbreg_0), .wm_out(WM_EX_MEM_0),
    .mem_to_reg_out(wb_0));
  pipeline_EX_MEM pipeline_ex_mem_2 (
    .ULA_result_in(ula_vet_2_c), .A_in(ra_1), .B_in(rb_1), .index_ra_in(pipeline_id_ex_2_index_ra_out),
    .wbreg_in(pipeline_id_ex_2_wbreg_out), .wm_in(pipeline_id_ex_2_wm_out),
    .mem_to_reg_in(pipeline_id_ex_2_mem_to_reg_out), .CLK(CLK), .ULA_result_out(ULA_1), .A_out(A_EX_MEM_1),
    .B_out(B_EX_MEM_1), .index_ra_out(index_ra_1), .wbreg_out(wbreg_1), .wm_out(WM_EX_MEM_1),
    .mem_to_reg_out(wb_1));
  pipeline_EX_MEM pipeline_ex_mem_3 (
    .ULA_result_in(ula_vet_3_c), .A_in(ra_2), .B_in(rb_2), .index_ra_in(pipeline_id_ex_3_index_ra_out),
    .wbreg_in(pipeline_id_ex_3_wbreg_out), .wm_in(pipeline_id_ex_3_wm_out),
    .mem_to_reg_in(pipeline_id_ex_3_mem_to_reg_out), .CLK(CLK), .ULA_result_out(ULA_2), .A_out(A_EX_MEM_2),
    .B_out(B_EX_MEM_2), .index_ra_out(index_ra_2), .wbreg_out(wbreg_2), .wm_out(WM_EX_MEM_2),
    .mem_to_reg_out(wb_2));
  pipeline_EX_MEM pipeline_ex_mem_4 (
    .ULA_result_in(ula_vet_4_c), .A_in(ra_3), .B_in(rb_3), .index_ra_in(pipeline_id_ex_4_index_ra_out),
    .wbreg_in(pipeline_id_ex_4_wbreg_out), .wm_in(pipeline_id_ex_4_wm_out),
    .mem_to_reg_in(pipeline_id_ex_4_mem_to_reg_out), .CLK(CLK), .ULA_result_out(ULA_3), .A_out(A_EX_MEM_3),
    .B_out(B_EX_MEM_3), .index_ra_out(index_ra_3), .wbreg_out(wbreg_3), .wm_out(WM_EX_MEM_3),
    .mem_to_reg_out(wb_3));
  Adder adder_1 (.a(8'h1), .b(B_EX_MEM_1), .out(adder_1_out));  // open: cin, cout
  Adder adder_2 (.a(8'h3), .b(B_EX_MEM_3), .out(adder_2_out));  // open: cin, cout
  Adder adder_3 (.a(8'h2), .b(B_EX_MEM_2), .out(adder_3_out));  // open: cin, cout
  // DualRAM dualram_1: pin names not known; wires that end beside it: B_EX_MEM_0, WM_EX_MEM_0, 1'b1, CLK, adder_1_out, WM_EX_MEM_1, 1'b1, CLK, A_EX_MEM_0, dualram_1_p10
  // DualRAM dualram_2: pin names not known; wires that end beside it: adder_3_out, WM_EX_MEM_2, 1'b1, CLK, adder_2_out, WM_EX_MEM_3, 1'b1, CLK, A_EX_MEM_2, dualram_2_p10
  Multiplexer #(.width(8)) multiplexer_6 (.in0(ULA_0), .in1(dualram_1_p10), .out(D_0), .sel(wb_0));
  Multiplexer #(.width(8)) multiplexer_7 (.in0(ULA_1), .in1(undriven), .out(D_1), .sel(wb_1));
  Multiplexer #(.width(8)) multiplexer_8 (.in0(ULA_2), .in1(dualram_2_p10), .out(D_2), .sel(wb_2));
  Multiplexer #(.width(8)) multiplexer_9 (.in0(ULA_3), .in1(undriven_2), .out(D_3), .sel(wb_3));

  // Other names for the same wires on the sheet: mem_reg = wb; mov_instru = is_mov_vet; movh[7:4] = IMM;
  //   movl[3:0] = IMM; ra_in[1:0] = ra; rb_in[1:0] = rb
endmodule

module ULA_vet (
  input  [7:0] A,
  input  [7:0] B,
  input  [1:0] OPULA,
  output [7:0] C
);

  wire [7:0] adder_1_out, and_1_out, subtractor_1_out;

  Adder adder_1 (.a(A), .b(B), .out(adder_1_out));  // open: cin, cout
  Subtractor subtractor_1 (.a(A), .b(B), .out(subtractor_1_out));  // open: bin, bout
  assign and_1_out = A & B;  // AND_Gate and_1, 8 bits wide
  Multiplexer #(.select(2), .width(8)) multiplexer_1 (
    .in0(adder_1_out), .in1(subtractor_1_out), .in2(and_1_out), .out(C), .sel(OPULA));  // open: in3
endmodule
